# Fritzing sketch Cableado del Siguelineas (saved by Fritzing 0.9.3b)
breadboards: 1

parts:
  U1 = QRD1114 [package=qrd1114]
  U2 = QRD1114 [package=qrd1114]
  U3 = ICL3232 [package=dil16]
  M1 = DC Motor
  R1 = Resistor [tolerance=±5% resistance=220 package=THT]
  R3 = Resistor [tolerance=±5% resistance=220 package=THT]
  R4 = Resistor [tolerance=±5% resistance=10k package=THT]
  R2 = Resistor [tolerance=±5% resistance=10k package=THT]
  Componente1 = iceZUM Alhambra
  BAT1 = BC9VPC [package=bc9vpc]
  M4 = DC Motor
  J1 = Power Jack [package=power_jack_pth]
  U4 = SWITCH-SPST-2 [package=switch-spst-vertical]

nets:
  N1: U1.E, U1.K, U2.E, U2.K, U3.C2+, U3.C2-, U3.R1OUT, U3.R1IN, Componente1.GD4, Componente1.GND
  N2: U1.C, R2.Pin_1, Componente1.D4, Componente1.V4
  N3: U1.A, R3.Pin_1
  N4: U2.C, R4.Pin_1, Componente1.D5, Componente1.V5
  N5: U2.A, R1.Pin_1
  N6: U3.V+, Componente1.D13
  N7: U3.C1-, M1.pin_1
  N8: U3.V-, Componente1.D12
  N9: U3.R2IN, M1.pin_2, J1.GND, U4.O
  N10: U3.T2IN, Componente1.D10
  N11: U3.T1IN, M4.pin_1
  N12: U3.T1OUT, Componente1.D11
  N13: U3.GND, M4.pin_2
  VCC: U3.VCC, R1.Pin_0, R3.Pin_0, R4.Pin_0, R2.Pin_0, Componente1.5V
  N14: BAT1.V+, U4.P
  N15: BAT1.V-, J1.GNDBREAK

custom parts:
  iceZUM Alhambra: Arduino/zum compatible Open FPGA electronic board. Synthesize hardware easily, using only open source tools
